// Logisim project TheLife.circ as structural Verilog: 8 circuits, main circuit Cell
module main (
);

  wire controller_1_tick, d_out, l_out, ok_out, r_out, transistor_1_out, u_out;
  wire [7:0] controlled_buffer_1_out;
  wire [15:0] controller_1_out_1, controller_1_out_2, controller_1_out_3, controller_1_out_4,
       controller_1_out_5, controller_1_out_6, controller_1_out_7, controller_1_out_8, controller_1_out_9,
       controller_1_out_10, controller_1_out_11, controller_1_out_12, controller_1_out_13,
       controller_1_out_14, controller_1_out_15, rows_plate_1_out_1, rows_plate_1_out_2, rows_plate_1_out_3,
       rows_plate_1_out_4, rows_plate_1_out_5, rows_plate_1_out_6, rows_plate_1_out_7, rows_plate_1_out_8,
       rows_plate_1_out_9, rows_plate_1_out_10, rows_plate_1_out_11, rows_plate_1_out_12,
       rows_plate_1_out_13, rows_plate_1_out_14, rows_plate_1_out_15;

  Button ok (.out(ok_out));
  assign controlled_buffer_1_out = ok_out ? 8'h5 : 8'bz;  // Controlled_Buffer controlled_buffer_1
  Transistor #(.\type ("n")) transistor_1 (.in(1'b0), .out(transistor_1_out), .gate(ok_out));
  Button l (.out(l_out));
  assign controlled_buffer_1_out = l_out ? 8'h4 : 8'bz;  // Controlled_Buffer controlled_buffer_2
  Transistor #(.\type ("n")) transistor_2 (.in(1'b0), .out(transistor_1_out), .gate(l_out));
  Transistor #(.\type ("n")) transistor_3 (.in(1'b0), .out(transistor_1_out), .gate(d_out));
  Button d (.out(d_out));
  assign controlled_buffer_1_out = d_out ? 8'h3 : 8'bz;  // Controlled_Buffer controlled_buffer_3
  Transistor #(.\type ("n")) transistor_4 (.in(1'b0), .out(transistor_1_out), .gate(u_out));
  Button u (.out(u_out));
  Transistor #(.\type ("n")) transistor_5 (.in(1'b0), .out(transistor_1_out), .gate(r_out));
  Button r (.out(r_out));
  assign controlled_buffer_1_out = r_out ? 8'h2 : 8'bz;  // Controlled_Buffer controlled_buffer_4
  assign controlled_buffer_1_out = u_out ? 8'h1 : 8'bz;  // Controlled_Buffer controlled_buffer_5
  Pull_Resistor #(.pull(1)) pull_resistor_1 (.node(transistor_1_out));
  DotMatrix #(.matrixcols(15), .matrixrows(16)) dotmatrix_1 (
    .col0(rows_plate_1_out_1), .col1(rows_plate_1_out_2), .col2(rows_plate_1_out_3),
    .col3(rows_plate_1_out_4), .col4(rows_plate_1_out_5), .col5(rows_plate_1_out_6),
    .col6(rows_plate_1_out_7), .col7(rows_plate_1_out_8), .col8(rows_plate_1_out_9),
    .col9(rows_plate_1_out_10), .col10(rows_plate_1_out_11), .col11(rows_plate_1_out_12),
    .col12(rows_plate_1_out_13), .col13(rows_plate_1_out_14), .col14(rows_plate_1_out_15));
  Rows_plate rows_plate_1 (
    .tick(controller_1_tick), .Pressed_1(controller_1_out_15), .Pressed_2(controller_1_out_14),
    .Pressed_3(controller_1_out_13), .Pressed_4(controller_1_out_12), .Pressed_5(controller_1_out_11),
    .Pressed_6(controller_1_out_10), .Pressed_7(controller_1_out_9), .Pressed_8(controller_1_out_8),
    .Pressed_9(controller_1_out_7), .Pressed_10(controller_1_out_6), .Pressed_11(controller_1_out_5),
    .Pressed_12(controller_1_out_4), .Pressed_13(controller_1_out_3), .Pressed_14(controller_1_out_2),
    .Pressed_15(controller_1_out_1), .out_1(rows_plate_1_out_1), .out_2(rows_plate_1_out_2),
    .out_3(rows_plate_1_out_3), .out_4(rows_plate_1_out_4), .out_5(rows_plate_1_out_5),
    .out_6(rows_plate_1_out_6), .out_7(rows_plate_1_out_7), .out_8(rows_plate_1_out_8),
    .out_9(rows_plate_1_out_9), .out_10(rows_plate_1_out_10), .out_11(rows_plate_1_out_11),
    .out_12(rows_plate_1_out_12), .out_13(rows_plate_1_out_13), .out_14(rows_plate_1_out_14),
    .out_15(rows_plate_1_out_15));
  Clock clock_1 ();  // open: out
  Controller controller_1 (
    .tick(controller_1_tick), .inp(controlled_buffer_1_out), .out_1(controller_1_out_1),
    .out_2(controller_1_out_2), .out_3(controller_1_out_3), .out_4(controller_1_out_4),
    .out_5(controller_1_out_5), .out_6(controller_1_out_6), .out_7(controller_1_out_7),
    .out_8(controller_1_out_8), .out_9(controller_1_out_9), .out_10(controller_1_out_10),
    .out_11(controller_1_out_11), .out_12(controller_1_out_12), .out_13(controller_1_out_13),
    .out_14(controller_1_out_14), .out_15(controller_1_out_15));
endmodule

module Cell (
  input  can_play,
  input  upper_center,
  input  upper_left,
  input  upper_right,
  input  left,
  input  right,
  input  bottom_left,
  input  bottom_right,
  input  bottom_center,
  input  pressed,
  input  tick,
  output State
);

  State_manager state_manager_1 (
    .can_play(can_play), .nb1(upper_center), .nb2(upper_left), .nb3(upper_right), .nb4(left), .nb5(right),
    .nb6(bottom_left), .nb7(bottom_right), .nb8(bottom_center), .user_s_hand(pressed), .tick(tick),
    .State(State));
endmodule

module State_manager (
  input  can_play,
  input  nb1,
  input  nb2,
  input  nb3,
  input  nb4,
  input  nb5,
  input  nb6,
  input  nb7,
  input  nb8,
  input  user_s_hand,
  input  tick,
  output State
);

  wire and_1_out, and_2_out, and_3_out, and_4_out, and_5_out, and_6_out, and_7_out, not_1_out, not_2_out,
       not_3_out, not_4_out, not_5_out, not_7_out, or_1_out, or_2_out, register_1_q;
  wire [1:0] adder_1_out, adder_2_out, adder_3_out, adder_4_out, adder_5_out, adder_6_out;
  wire [2:0] adder_7_out;
  wire [2:2] adder_5_cout, adder_6_cout;

  Adder #(.width(1)) adder_1 (.a(nb1), .b(nb2), .out(adder_1_out[0]), .cout(adder_1_out[1]));  // open: cin
  Adder #(.width(1)) adder_2 (.a(nb3), .b(nb4), .out(adder_2_out[0]), .cout(adder_2_out[1]));  // open: cin
  Adder #(.width(1)) adder_3 (.a(nb5), .b(nb6), .out(adder_3_out[0]), .cout(adder_3_out[1]));  // open: cin
  Adder #(.width(1)) adder_4 (.a(nb7), .b(nb8), .out(adder_4_out[0]), .cout(adder_4_out[1]));  // open: cin
  Adder #(.width(2)) adder_5 (
    .a(adder_1_out), .b(adder_2_out), .out(adder_5_out), .cout(adder_5_cout[2]));  // open: cin
  Adder #(.width(2)) adder_6 (
    .a(adder_3_out), .b(adder_4_out), .out(adder_6_out), .cout(adder_6_cout[2]));  // open: cin
  Adder #(.width(3)) adder_7 (
    .a({adder_5_cout[2], adder_5_out}), .b({adder_6_cout[2], adder_6_out}), .out(adder_7_out));  // open: cin, cout
  not not_1 (not_1_out, adder_7_out[2]);
  not not_2 (not_2_out, adder_7_out[0]);
  and and_1 (and_1_out, adder_7_out[0], adder_7_out[1], not_1_out);
  and and_2 (and_2_out, not_1_out, adder_7_out[1], not_2_out);
  and and_3 (and_3_out, user_s_hand, tick);
  or or_1 (or_1_out, and_1_out, and_2_out);
  not not_3 (not_3_out, register_1_q);
  and and_4 (and_4_out, can_play, and_5_out);
  and and_5 (and_5_out, and_1_out, not_3_out);
  and and_6 (and_6_out, can_play, and_7_out);
  and and_7 (and_7_out, register_1_q, or_1_out);
  or or_2 (or_2_out, and_4_out, and_6_out, and_3_out);
  Register #(.width(1), .trigger("falling")) register_1 (.D(or_2_out), .Q(register_1_q), .clk(tick));  // open: en, clr
  not not_4 (not_4_out, register_1_q);
  not not_5 (not_5_out, not_7_out);
  not not_6 (State, not_5_out);
  not not_7 (not_7_out, not_4_out);

  // Notes on the sheet:
  //   Соседи
  //   3 живые
  //   2 живые
  //   Команда на смену состояния
  //   Оживание по правилам + нет команд от юзера
  //   Отрицание для смены состояния
  //   Продолжение существования
endmodule

module Row_of_cells (
  input  [15:0] Top,
  input  can_play,
  input  tick,
  input  [15:0] Down,
  input  [15:0] Pressed,
  output [15:0] Display
);

  Cell cell_1 (
    .upper_center(Top[0]), .upper_left(Top[15]), .upper_right(Top[1]), .left(Display[15]),
    .right(Display[1]), .bottom_left(Down[15]), .bottom_right(Down[1]), .bottom_center(Down[0]),
    .pressed(Pressed[0]), .tick(tick), .State(Display[0]), .can_play(can_play));
  Cell cell_2 (
    .upper_center(Top[1]), .upper_left(Top[0]), .upper_right(Top[2]), .left(Display[0]), .right(Display[2]),
    .bottom_left(Down[0]), .bottom_right(Down[2]), .bottom_center(Down[1]), .pressed(Pressed[1]),
    .tick(tick), .State(Display[1]), .can_play(can_play));
  Cell cell_3 (
    .upper_center(Top[2]), .upper_left(Top[1]), .upper_right(Top[3]), .left(Display[1]), .right(Display[3]),
    .bottom_left(Down[1]), .bottom_right(Down[3]), .bottom_center(Down[2]), .pressed(Pressed[2]),
    .tick(tick), .State(Display[2]), .can_play(can_play));
  Cell cell_4 (
    .upper_center(Top[3]), .upper_left(Top[2]), .upper_right(Top[4]), .left(Display[2]), .right(Display[4]),
    .bottom_left(Down[2]), .bottom_right(Down[4]), .bottom_center(Down[3]), .pressed(Pressed[3]),
    .tick(tick), .State(Display[3]), .can_play(can_play));
  Cell cell_5 (
    .upper_center(Top[4]), .upper_left(Top[3]), .upper_right(Top[5]), .left(Display[3]), .right(Display[5]),
    .bottom_left(Down[3]), .bottom_right(Down[5]), .bottom_center(Down[4]), .pressed(Pressed[4]),
    .tick(tick), .State(Display[4]), .can_play(can_play));
  Cell cell_6 (
    .upper_center(Top[5]), .upper_left(Top[4]), .upper_right(Top[6]), .left(Display[4]), .right(Display[6]),
    .bottom_left(Down[4]), .bottom_right(Down[6]), .bottom_center(Down[5]), .pressed(Pressed[5]),
    .tick(tick), .State(Display[5]), .can_play(can_play));
  Cell cell_7 (
    .upper_center(Top[6]), .upper_left(Top[5]), .upper_right(Top[7]), .left(Display[5]), .right(Display[7]),
    .bottom_left(Down[5]), .bottom_right(Down[7]), .bottom_center(Down[6]), .pressed(Pressed[6]),
    .tick(tick), .State(Display[6]), .can_play(can_play));
  Cell cell_8 (
    .upper_center(Top[7]), .upper_left(Top[6]), .upper_right(Top[8]), .left(Display[6]), .right(Display[8]),
    .bottom_left(Down[6]), .bottom_right(Down[8]), .bottom_center(Down[7]), .pressed(Pressed[7]),
    .tick(tick), .State(Display[7]), .can_play(can_play));
  Cell cell_9 (
    .upper_center(Top[8]), .upper_left(Top[7]), .upper_right(Top[9]), .left(Display[7]), .right(Display[9]),
    .bottom_left(Down[7]), .bottom_right(Down[9]), .bottom_center(Down[8]), .pressed(Pressed[8]),
    .tick(tick), .State(Display[8]), .can_play(can_play));
  Cell cell_10 (
    .upper_center(Top[9]), .upper_left(Top[8]), .upper_right(Top[10]), .left(Display[8]),
    .right(Display[10]), .bottom_left(Down[8]), .bottom_right(Down[10]), .bottom_center(Down[9]),
    .pressed(Pressed[9]), .tick(tick), .State(Display[9]), .can_play(can_play));
  Cell cell_11 (
    .upper_center(Top[10]), .upper_left(Top[9]), .upper_right(Top[11]), .left(Display[9]),
    .right(Display[11]), .bottom_left(Down[9]), .bottom_right(Down[11]), .bottom_center(Down[10]),
    .pressed(Pressed[10]), .tick(tick), .State(Display[10]), .can_play(can_play));
  Cell cell_12 (
    .upper_center(Top[11]), .upper_left(Top[10]), .upper_right(Top[12]), .left(Display[10]),
    .right(Display[12]), .bottom_left(Down[10]), .bottom_right(Down[12]), .bottom_center(Down[11]),
    .pressed(Pressed[11]), .tick(tick), .State(Display[11]), .can_play(can_play));
  Cell cell_13 (
    .upper_center(Top[12]), .upper_left(Top[11]), .upper_right(Top[13]), .left(Display[11]),
    .right(Display[13]), .bottom_left(Down[11]), .bottom_right(Down[13]), .bottom_center(Down[12]),
    .pressed(Pressed[12]), .tick(tick), .State(Display[12]), .can_play(can_play));
  Cell cell_14 (
    .upper_center(Top[13]), .upper_left(Top[12]), .upper_right(Top[14]), .left(Display[12]),
    .right(Display[14]), .bottom_left(Down[12]), .bottom_right(Down[14]), .bottom_center(Down[13]),
    .pressed(Pressed[13]), .tick(tick), .State(Display[13]), .can_play(can_play));
  Cell cell_15 (
    .upper_center(Top[14]), .upper_left(Top[13]), .upper_right(Top[15]), .left(Display[13]),
    .right(Display[15]), .bottom_left(Down[13]), .bottom_right(Down[15]), .bottom_center(Down[14]),
    .pressed(Pressed[14]), .tick(tick), .State(Display[14]), .can_play(can_play));
  Cell cell_16 (
    .upper_center(Top[15]), .upper_left(Top[14]), .upper_right(Top[0]), .left(Display[14]),
    .right(Display[0]), .bottom_left(Down[14]), .bottom_right(Down[0]), .bottom_center(Down[15]),
    .pressed(Pressed[15]), .tick(tick), .State(Display[15]), .can_play(can_play));
  counter counter_1 (
    .nb1(Display[0]), .nb2(Display[1]), .nb3(Display[2]), .nb4(Display[3]), .nb5(Display[4]),
    .nb6(Display[5]), .nb7(Display[6]), .nb8(Display[7]), .nb1_2(Display[8]), .nb2_2(Display[9]),
    .nb3_2(Display[10]), .nb4_2(Display[11]), .nb5_2(Display[12]), .nb6_2(Display[13]), .nb7_2(Display[14]),
    .nb8_2(Display[15]));  // open: total

  // Notes on the sheet:
  //   Top row of neighbors ->
  //   Bottom row of neighbors
  //   User's impact
  //   can play
  //   can play
  //   can play
  //   can play
  //   can play
  //   can play
  //   can play
  //   can play
endmodule

module Rows_plate (
  input  tick,
  input  [15:0] Pressed_1,
  input  [15:0] Pressed_2,
  input  [15:0] Pressed_3,
  input  [15:0] Pressed_4,
  input  [15:0] Pressed_5,
  input  [15:0] Pressed_6,
  input  [15:0] Pressed_7,
  input  [15:0] Pressed_8,
  input  [15:0] Pressed_9,
  input  [15:0] Pressed_10,
  input  [15:0] Pressed_11,
  input  [15:0] Pressed_12,
  input  [15:0] Pressed_13,
  input  [15:0] Pressed_14,
  input  [15:0] Pressed_15,
  output [15:0] out_1,
  output [15:0] out_2,
  output [15:0] out_3,
  output [15:0] out_4,
  output [15:0] out_5,
  output [15:0] out_6,
  output [15:0] out_7,
  output [15:0] out_8,
  output [15:0] out_9,
  output [15:0] out_10,
  output [15:0] out_11,
  output [15:0] out_12,
  output [15:0] out_13,
  output [15:0] out_14,
  output [15:0] out_15
);

  wire pull_resistor_1_node;

  Pull_Resistor #(.pull(1)) pull_resistor_1 (.node(pull_resistor_1_node));
  Row_of_cells row_of_cells_1 (
    .tick(tick), .Pressed(Pressed_1), .Display(out_1), .Top(out_15), .Down(out_2),
    .can_play(pull_resistor_1_node));
  Row_of_cells row_of_cells_2 (
    .tick(tick), .Pressed(Pressed_2), .Display(out_2), .Top(out_1), .Down(out_3),
    .can_play(pull_resistor_1_node));
  Row_of_cells row_of_cells_3 (
    .tick(tick), .Pressed(Pressed_3), .Display(out_3), .Top(out_2), .Down(out_4),
    .can_play(pull_resistor_1_node));
  Row_of_cells row_of_cells_4 (
    .tick(tick), .Pressed(Pressed_4), .Display(out_4), .Top(out_3), .Down(out_5),
    .can_play(pull_resistor_1_node));
  Row_of_cells row_of_cells_5 (
    .tick(tick), .Pressed(Pressed_5), .Display(out_5), .Top(out_4), .Down(out_6),
    .can_play(pull_resistor_1_node));
  Row_of_cells row_of_cells_6 (
    .tick(tick), .Pressed(Pressed_6), .Display(out_6), .Top(out_5), .Down(out_7),
    .can_play(pull_resistor_1_node));
  Row_of_cells row_of_cells_7 (
    .tick(tick), .Pressed(Pressed_7), .Display(out_7), .Top(out_6), .Down(out_8),
    .can_play(pull_resistor_1_node));
  Row_of_cells row_of_cells_8 (
    .tick(tick), .Pressed(Pressed_8), .Display(out_8), .Top(out_7), .Down(out_9),
    .can_play(pull_resistor_1_node));
  Row_of_cells row_of_cells_9 (
    .tick(tick), .Pressed(Pressed_9), .Display(out_9), .Top(out_8), .Down(out_10),
    .can_play(pull_resistor_1_node));
  Row_of_cells row_of_cells_10 (
    .tick(tick), .Pressed(Pressed_10), .Display(out_10), .Top(out_9), .Down(out_11),
    .can_play(pull_resistor_1_node));
  Row_of_cells row_of_cells_11 (
    .tick(tick), .Pressed(Pressed_11), .Display(out_11), .Top(out_10), .Down(out_12),
    .can_play(pull_resistor_1_node));
  Row_of_cells row_of_cells_12 (
    .tick(tick), .Pressed(Pressed_12), .Display(out_12), .Top(out_11), .Down(out_13),
    .can_play(pull_resistor_1_node));
  Row_of_cells row_of_cells_13 (
    .tick(tick), .Pressed(Pressed_13), .Display(out_13), .Top(out_12), .Down(out_14),
    .can_play(pull_resistor_1_node));
  Row_of_cells row_of_cells_14 (
    .tick(tick), .Pressed(Pressed_14), .Display(out_14), .Top(out_13), .Down(out_15),
    .can_play(pull_resistor_1_node));
  Row_of_cells row_of_cells_15 (
    .tick(tick), .Pressed(Pressed_15), .Display(out_15), .Top(out_14), .Down(out_1),
    .can_play(pull_resistor_1_node));
endmodule

module Controller (
  input  [7:0] inp,
  output [15:0] out_1,
  output [15:0] out_2,
  output [15:0] out_3,
  output [15:0] out_4,
  output [15:0] out_5,
  output [15:0] out_6,
  output [15:0] out_7,
  output [15:0] out_8,
  output [15:0] out_9,
  output [15:0] out_10,
  output [15:0] out_11,
  output [15:0] out_12,
  output [15:0] out_13,
  output [15:0] out_14,
  output [15:0] out_15,
  output tick
);

  wire and_2_out, cdm_8_mark5_1_p4, cdm_8_mark5_1_p5, cdm_8_mark5_1_p7, cdm_8_mark5_1_p8, cdm_8_mark5_1_p9,
       cdm_8_mark5_1_p10, cdm_8_mark5_1_p11, cdm_8_mark5_1_p12, cdm_8_mark5_1_p13, clk, d_out,
       decoder_1_out0, decoder_1_out1, decoder_2_out0, decoder_2_out1, I_O_0_out, IAck, IOsel, IRQ, l_out,
       nor_1_out, nor_2_out, not_1_out, not_2_out, not_3_out, not_4_out, ok_out, r_out, READwrite,
       transistor_1_out, u_out, undriven;
  wire [2:0] vec;
  wire [3:0] IOaddr;
  wire [6:0] controlled_buffer_9_out;
  wire [7:0] cdm_8_mark5_1_p15_2, cdm_8_mark5_1_p16, cdm_8_mark5_1_p17, controlled_buffer_3_out, IOdat;
  wire [7:4] cdm_8_mark5_1_p15;

  Clock clock_1 (.out(clk));
  // Probe on cdm_8_mark5_1_p8
  // Probe on cdm_8_mark5_1_p7
  // Probe on cdm_8_mark5_1_p5
  // Probe on cdm_8_mark5_1_p4
  // Probe on cdm_8_mark5_1_p9
  and and_1 (IOsel, ~cdm_8_mark5_1_p15[4], cdm_8_mark5_1_p15[5], cdm_8_mark5_1_p15[6], cdm_8_mark5_1_p15[7], decoder_1_out1);  // AND_Gate
  // Probe on cdm_8_mark5_1_p11
  // Probe on cdm_8_mark5_1_p10
  // CdM_8_mark5 cdm_8_mark5_1: pin names not known; wires that end beside it: IRQ, vec, IAck, cdm_8_mark5_1_p4, cdm_8_mark5_1_p5, clk, cdm_8_mark5_1_p7, cdm_8_mark5_1_p8, cdm_8_mark5_1_p9, cdm_8_mark5_1_p10, cdm_8_mark5_1_p11, cdm_8_mark5_1_p12, cdm_8_mark5_1_p13, READwrite, {cdm_8_mark5_1_p15_2, cdm_8_mark5_1_p15, IOaddr}, cdm_8_mark5_1_p16, cdm_8_mark5_1_p17, 1'b0
  not not_1 (not_1_out, transistor_1_out);
  not not_2 (not_2_out, undriven);
  Decoder #(.disabled(0)) decoder_1 (
    .out0(decoder_1_out0), .out1(decoder_1_out1), .sel(cdm_8_mark5_1_p12), .en(cdm_8_mark5_1_p13));
  not not_3 (not_3_out, READwrite);
  assign IOdat = not_3_out ? cdm_8_mark5_1_p16 : 8'bz;  // Controlled_Buffer controlled_buffer_1
  assign cdm_8_mark5_1_p17 = READwrite ? IOdat : 8'bz;  // Controlled_Buffer controlled_buffer_2
  Transistor #(.\type ("n")) transistor_1 (.in(1'b0), .out(transistor_1_out), .gate(ok_out));
  Button ok (.out(ok_out));
  assign controlled_buffer_3_out = ok_out ? 8'h5 : 8'bz;  // Controlled_Buffer controlled_buffer_3
  nor nor_1 (nor_1_out, transistor_1_out, not_1_out);
  nor nor_2 (nor_2_out, undriven, not_2_out);
  // Probe on {cdm_8_mark5_1_p15, IOaddr}
  and and_2 (and_2_out, decoder_1_out1, ~IOsel);  // AND_Gate
  Transistor #(.\type ("n")) transistor_2 (.in(1'b0), .out(transistor_1_out), .gate(l_out));
  Button l (.out(l_out));
  assign controlled_buffer_3_out = l_out ? 8'h4 : 8'bz;  // Controlled_Buffer controlled_buffer_4
  not not_4 (not_4_out, clk);
  Transistor #(.\type ("n")) transistor_3 (.in(1'b0), .out(transistor_1_out), .gate(u_out));
  Button u (.out(u_out));
  Transistor #(.\type ("n")) transistor_4 (.in(1'b0), .out(transistor_1_out), .gate(d_out));
  Button d (.out(d_out));
  assign controlled_buffer_3_out = u_out ? 8'h1 : 8'bz;  // Controlled_Buffer controlled_buffer_5
  assign controlled_buffer_3_out = d_out ? 8'h3 : 8'bz;  // Controlled_Buffer controlled_buffer_6
  // Probe on IOdat
  RAM ram_1 (
    .addr({cdm_8_mark5_1_p15, IOaddr}), .data(IOdat), .sel(and_2_out), .clk(not_4_out), .ld(READwrite));  // open: clr
  ROM #(.addrWidth(16)) rom_1 (
    .addr({cdm_8_mark5_1_p15_2, cdm_8_mark5_1_p15, IOaddr}), .data(IOdat), .sel(decoder_1_out0));
  Pull_Resistor #(.pull(1)) pull_resistor_1 (.node(transistor_1_out));
  Transistor #(.\type ("n")) transistor_5 (.in(1'b0), .out(transistor_1_out), .gate(r_out));
  Button r (.out(r_out));
  assign controlled_buffer_3_out = r_out ? 8'h2 : 8'bz;  // Controlled_Buffer controlled_buffer_7
  and I_O_0 (I_O_0_out, IOsel, ~IOaddr[0], ~IOaddr[1], ~IOaddr[2], ~IOaddr[3]);  // AND_Gate
  Decoder #(.disabled(0)) decoder_2 (.out0(decoder_2_out0), .out1(decoder_2_out1), .sel(READwrite), .en(I_O_0_out));
  OutputLogic outputlogic_1 (
    .I_O_addr(IOaddr), .I_O_sel(IOsel), .Read_write(READwrite), .I_O_dat(IOdat), .row(out_1),
    .o_number(4'b0001));
  assign IOdat = decoder_2_out1 ? controlled_buffer_3_out : 8'bz;  // Controlled_Buffer controlled_buffer_8
  assign {controlled_buffer_9_out, tick} = decoder_2_out0 ? IOdat : 8'bz;  // Controlled_Buffer controlled_buffer_9
  Pull_Resistor pull_resistor_2 (.node(tick));
  OutputLogic outputlogic_2 (
    .I_O_addr(IOaddr), .I_O_sel(IOsel), .Read_write(READwrite), .I_O_dat(IOdat), .row(out_2),
    .o_number(4'b0010));
  OutputLogic outputlogic_3 (
    .I_O_addr(IOaddr), .I_O_sel(IOsel), .Read_write(READwrite), .I_O_dat(IOdat), .row(out_3),
    .o_number(4'b0011));
  OutputLogic outputlogic_4 (
    .I_O_addr(IOaddr), .I_O_sel(IOsel), .Read_write(READwrite), .I_O_dat(IOdat), .row(out_4),
    .o_number(4'b0100));
  OutputLogic outputlogic_5 (
    .I_O_addr(IOaddr), .I_O_sel(IOsel), .Read_write(READwrite), .I_O_dat(IOdat), .row(out_5),
    .o_number(4'b0101));
  OutputLogic outputlogic_6 (
    .I_O_addr(IOaddr), .I_O_sel(IOsel), .Read_write(READwrite), .I_O_dat(IOdat), .row(out_6),
    .o_number(4'b0110));
  OutputLogic outputlogic_7 (
    .I_O_addr(IOaddr), .I_O_sel(IOsel), .Read_write(READwrite), .I_O_dat(IOdat), .row(out_7),
    .o_number(4'b0111));
  OutputLogic outputlogic_8 (
    .I_O_addr(IOaddr), .I_O_sel(IOsel), .Read_write(READwrite), .I_O_dat(IOdat), .row(out_8),
    .o_number(4'b1000));
  OutputLogic outputlogic_9 (
    .I_O_addr(IOaddr), .I_O_sel(IOsel), .Read_write(READwrite), .I_O_dat(IOdat), .row(out_9),
    .o_number(4'b1001));
  OutputLogic outputlogic_10 (
    .I_O_addr(IOaddr), .I_O_sel(IOsel), .Read_write(READwrite), .I_O_dat(IOdat), .row(out_10),
    .o_number(4'b1010));
  OutputLogic outputlogic_11 (
    .I_O_addr(IOaddr), .I_O_sel(IOsel), .Read_write(READwrite), .I_O_dat(IOdat), .row(out_11),
    .o_number(4'b1011));
  OutputLogic outputlogic_12 (
    .I_O_addr(IOaddr), .I_O_sel(IOsel), .Read_write(READwrite), .I_O_dat(IOdat), .row(out_12),
    .o_number(4'b1100));
  OutputLogic outputlogic_13 (
    .I_O_addr(IOaddr), .I_O_sel(IOsel), .Read_write(READwrite), .I_O_dat(IOdat), .row(out_13),
    .o_number(4'b1101));
  OutputLogic outputlogic_14 (
    .I_O_addr(IOaddr), .I_O_sel(IOsel), .Read_write(READwrite), .I_O_dat(IOdat), .row(out_14),
    .o_number(4'b1110));
  OutputLogic outputlogic_15 (
    .I_O_addr(IOaddr), .I_O_sel(IOsel), .Read_write(READwrite), .I_O_dat(IOdat), .row(out_15),
    .o_number(4'b1111));

  // Notes on the sheet:
  //   contents of rom_1 (hex, n*v repeats v):
  //   d0 f d1 e0 d2 1 d3 0 ac 12 a9 d6 7b 0 d0 e1 d2 f a e4 9 d3 0 a3 a3 8c 8a ee f6 d0 e0 d1 1 d2 0 e0 5
  //   a1 a2 ee fb e0 3b d3 e0 bf f e0 33 d6 95 0 8b e1 6 d6 dd 0 ee 25 8b e1 6 d6 9c 0 ee 1d 8b e1 6 d6 f2
  //   0 ee 15 8b e1 6 d6 ab 0 ee d 8b e1 6 d6 66 0 ee 5 8b e1 2 d7 d6 7b 0 ee c5 d7 d0 1 d1 30 d2 1e a e4
  //   c c2 b2 b7 5b a7 c6 8c 8d 8a ee f3 d7 d0 e1 d1 1 d2 f a e4 b b7 a3 8d b7 a3 8d 8c 8a ee f4 d0 e0 d1
  //   1 a1 a2 d7 d0 0 b1 d2 1 16 d7 bb 93 e3 8 d3 80 d6 ba 0 ee 4 d6 12 1 d7 bb 97 e3 8 d3 1 d6 ba 0 ee 4
  //   d6 12 1 d7 d6 17 1 d1 1 d0 0 b0 41 e1 8 8e 8c d1 0 a4 ee 6 8a 88 d1 0 a4 f e5 6 d0 80 a8 ee 4 d0 1
  //   a8 d7 d3 2 d0 0 b1 77 e5 8 d3 1c d6 7 1 ee 6 d3 fe d6 7 dd 0 0 1b d0 0 b1 7d e5 8 d3 e4 d6 7 1 ee 6
  //   d3 2 d6 7 1 d7 d6 17 1 1e a8 d0 0 b2 1e a2 d7 d2 1 16 ab d7 b8 d1 0 a9 d7
  //   read
endmodule

module OutputLogic (
  input  [3:0] I_O_addr,
  input  I_O_sel,
  input  Read_write,
  input  [7:0] I_O_dat,
  input  [3:0] o_number,
  output [15:0] row
);

  wire and_1_out, and_2_out, and_3_out, decoder_1_out0, I_O___number_out, not_1_out, not_2_out, not_3_out,
       not_4_out, not_5_out, not_6_out, not_7_out, not_8_out, not_9_out, not_10_out, register_3_q,
       xnor_1_out, xnor_2_out, xnor_3_out, xnor_4_out;
  wire [7:0] controlled_buffer_1_out;

  xnor xnor_1 (xnor_1_out, I_O_addr[0], o_number[0]);
  xnor xnor_2 (xnor_2_out, I_O_addr[1], o_number[1]);
  xnor xnor_3 (xnor_3_out, I_O_addr[2], o_number[2]);
  xnor xnor_4 (xnor_4_out, I_O_addr[3], o_number[3]);
  and I_O___number (I_O___number_out, I_O_sel, xnor_1_out, xnor_2_out, xnor_3_out, xnor_4_out);
  Decoder #(.disabled(0)) decoder_1 (.out0(decoder_1_out0), .sel(Read_write), .en(I_O___number_out));  // open: out1
  not not_1 (not_1_out, decoder_1_out0);
  not not_2 (not_2_out, not_1_out);
  not not_3 (not_3_out, not_2_out);
  not not_4 (not_4_out, not_3_out);
  assign controlled_buffer_1_out = decoder_1_out0 ? I_O_dat : 8'bz;  // Controlled_Buffer controlled_buffer_1
  Register register_1 (.D(controlled_buffer_1_out), .Q(row[15:8]), .clk(and_1_out));  // open: en, clr
  and and_1 (and_1_out, not_10_out, not_4_out);
  Register register_2 (.D(controlled_buffer_1_out), .Q(row[7:0]), .clk(and_2_out));  // open: en, clr
  not not_5 (not_5_out, not_8_out);
  not not_6 (not_6_out, decoder_1_out0);
  not not_7 (not_7_out, not_6_out);
  not not_8 (not_8_out, not_7_out);
  and and_2 (and_2_out, not_5_out, register_3_q);
  not not_9 (not_9_out, register_3_q);
  and and_3 (and_3_out, not_9_out, decoder_1_out0);
  not not_10 (not_10_out, register_3_q);
  Register #(.width(1), .trigger("falling")) register_3 (
    .D(and_3_out), .Q(register_3_q), .clk(decoder_1_out0));  // open: en, clr
endmodule

module counter (
  input  nb1,
  input  nb2,
  input  nb3,
  input  nb4,
  input  nb5,
  input  nb6,
  input  nb7,
  input  nb8,
  input  nb1_2,
  input  nb2_2,
  input  nb3_2,
  input  nb4_2,
  input  nb5_2,
  input  nb6_2,
  input  nb7_2,
  input  nb8_2,
  output [7:0] total
);

  wire undriven, undriven_2, undriven_3, undriven_4, undriven_5, undriven_6, undriven_7, undriven_8,
       undriven_9, undriven_10;
  wire [1:0] adder_1_out, adder_2_out, adder_3_out, adder_4_out, adder_5_out, adder_6_out, adder_7_out,
       adder_8_out, adder_9_out, adder_10_out, adder_11_out, adder_12_out, adder_18_out, adder_22_out,
       adder_24_out, adder_26_out, adder_27_out;
  wire [1:1] adder_16_out, adder_20_out;
  wire [2:0] adder_13_out, adder_14_out;
  wire [2:2] adder_9_cout, adder_10_cout, adder_11_cout, adder_12_cout;

  Adder #(.width(1)) adder_1 (.a(nb1), .b(nb2), .out(adder_1_out[0]), .cout(adder_1_out[1]));  // open: cin
  Adder #(.width(1)) adder_2 (.a(nb3), .b(nb4), .out(adder_2_out[0]), .cout(adder_2_out[1]));  // open: cin
  Adder #(.width(1)) adder_3 (.a(nb5), .b(nb6), .out(adder_3_out[0]), .cout(adder_3_out[1]));  // open: cin
  Adder #(.width(1)) adder_4 (.a(nb7), .b(nb8), .out(adder_4_out[0]), .cout(adder_4_out[1]));  // open: cin
  Adder #(.width(1)) adder_5 (.a(nb1_2), .b(nb2_2), .out(adder_5_out[0]), .cout(adder_5_out[1]));  // open: cin
  Adder #(.width(1)) adder_6 (.a(nb3_2), .b(nb4_2), .out(adder_6_out[0]), .cout(adder_6_out[1]));  // open: cin
  Adder #(.width(1)) adder_7 (.a(nb5_2), .b(nb6_2), .out(adder_7_out[0]), .cout(adder_7_out[1]));  // open: cin
  Adder #(.width(1)) adder_8 (.a(nb7_2), .b(nb8_2), .out(adder_8_out[0]), .cout(adder_8_out[1]));  // open: cin
  Adder #(.width(2)) adder_9 (
    .a(adder_1_out), .b(adder_2_out), .out(adder_9_out), .cout(adder_9_cout[2]));  // open: cin
  Adder #(.width(2)) adder_10 (
    .a(adder_3_out), .b(adder_4_out), .out(adder_10_out), .cout(adder_10_cout[2]));  // open: cin
  Adder #(.width(2)) adder_11 (
    .a(adder_5_out), .b(adder_6_out), .out(adder_11_out), .cout(adder_11_cout[2]));  // open: cin
  Adder #(.width(2)) adder_12 (
    .a(adder_7_out), .b(adder_8_out), .out(adder_12_out), .cout(adder_12_cout[2]));  // open: cin
  Adder #(.width(3)) adder_13 (
    .a({adder_9_cout[2], adder_9_out}), .b({adder_10_cout[2], adder_10_out}), .out(adder_13_out));  // open: cin, cout
  Adder #(.width(3)) adder_14 (
    .a({adder_11_cout[2], adder_11_out}), .b({adder_12_cout[2], adder_12_out}), .out(adder_14_out));  // open: cin, cout
  Adder #(.width(3)) adder_15 (.a(adder_13_out), .b(adder_14_out), .out(total[2:0]), .cout(total[3]));  // open: cin
  Adder #(.width(1)) adder_16 (
    .a(undriven), .b(undriven_3), .out(adder_16_out[1]), .cout(adder_16_out[1]));  // open: cin
  Adder #(.width(1)) adder_17 (
    .a(undriven_3), .b(undriven_5), .out(adder_16_out[1]), .cout(adder_16_out[1]));  // open: cin
  Adder #(.width(1)) adder_18 (
    .a(undriven_5), .b(undriven_9), .out(adder_18_out[0]), .cout(adder_18_out[1]));  // open: cin
  Adder #(.width(1)) adder_19 (
    .a(undriven_9), .b(undriven_10), .out(adder_18_out[1]), .cout(adder_18_out[1]));  // open: cin
  Adder #(.width(1)) adder_20 (
    .a(undriven_6), .b(undriven_7), .out(adder_20_out[1]), .cout(adder_20_out[1]));  // open: cin
  Adder #(.width(1)) adder_21 (
    .a(undriven_6), .b(undriven_7), .out(adder_20_out[1]), .cout(adder_20_out[1]));  // open: cin
  Adder #(.width(1)) adder_22 (
    .a(undriven_4), .b(undriven_2), .out(adder_22_out[0]), .cout(adder_22_out[1]));  // open: cin
  Adder #(.width(1)) adder_23 (
    .a(undriven_8), .b(undriven_4), .out(adder_22_out[1]), .cout(adder_22_out[1]));  // open: cin
  Adder #(.width(2)) adder_24 (
    .a({2{adder_16_out[1]}}), .b(adder_18_out), .out(adder_24_out), .cout(adder_24_out[0]));  // open: cin
  Adder #(.width(2)) adder_25 (
    .a({2{adder_16_out[1]}}), .b({2{adder_18_out[1]}}), .out(adder_24_out), .cout(adder_24_out[0]));  // open: cin
  Adder #(.width(2)) adder_26 (
    .a({2{adder_20_out[1]}}), .b(adder_22_out), .out(adder_26_out), .cout(adder_27_out[0]));  // open: cin
  Adder #(.width(2)) adder_27 (
    .a({2{adder_20_out[1]}}), .b({2{adder_22_out[1]}}), .out(adder_27_out), .cout(adder_27_out[0]));  // open: cin
  // Pins of 1 and 2 bits meet at adder_27_out
  // Pins of 1 and 2 bits meet at adder_24_out

  assign total[7:4] = 4'b0000;

  // Notes on the sheet:
  //   Соседи
  //   Соседи
endmodule
